// Digital circuit tom-1.dig as structural Verilog
module tom_1 (
  input  clk,
  input  [7:0] in_2,
  input  [7:0] in_3,
  input  in_6,
  input  in_7,
  input  [15:0] in_8,
  output pulse,
  output clk_2
);

  wire and_1_out, and_2_out, and_3_out, and_4_out, and_5_out, and_6_out, and_7_out, decoder_1_out_0,
       decoder_1_out_1, decoder_1_out_2, decoder_1_out_3, delay_1_out, driver_1_out, nclk, not_1_out,
       not_2_out, not_4_out, not_5_out, not_6_out, not_7_out, npulse, nreset, nTOS_eq__eq_0_nis0, xor_1_out;
  wire [1:0] ROM_d_2;
  wire [7:0] driver_2_out, driver_2_out_2, driverinvsel_1_out, driverinvsel_1_out_2, I_O_LOW_p3,
       PROGRAM_COUNTER_pc, PROGRAM_COUNTER_pc_2, pulldown_1_out, pulldown_1_out_2, ROM_d, TOS_HIGH_out,
       TOS_LOW_out;
  wire [8:0] D_REGISTER_q;
  wire [15:0] CTRL_2_p3, multiplexer_1_out;
  wire [15:8] I_O_HIGH_p3;

  not not_1 (not_1_out, nTOS_eq__eq_0_nis0);
  and and_1 (and_1_out, not_1_out, clk, ROM_d[7]);
  Reset reset_1 (.out(nreset));
  Delay delay_1 (.in(nreset), .out(delay_1_out));
  xor xor_1 (xor_1_out, nreset, and_1_out);
  Multiplexer #(.Bits(16)) multiplexer_1 (
    .sel(delay_1_out), .in_0({16{1'b0}}), .in_1({pulldown_1_out, pulldown_1_out_2}), .out(multiplexer_1_out));
  // Probe on multiplexer_1_out
  tom_1_pc PROGRAM_COUNTER (
    .clk(npulse), .\input (multiplexer_1_out), .nLOAD(xor_1_out),
    .pc({PROGRAM_COUNTER_pc_2, PROGRAM_COUNTER_pc}));
  Break break_1 (.brk(driver_1_out));
  assign driver_1_out = in_7 ? npulse : 1'bz;  // Driver driver_1
  // tom_1_ctrl CTRL: pin names not known; wires that end beside it: npulse, PROGRAM_COUNTER_pc, CTRL_2_p3[7:0]
  // tom_1_ctrl CTRL_2: pin names not known; wires that end beside it: npulse, PROGRAM_COUNTER_pc_2, CTRL_2_p3[15:8]
  Break BREAK_2 (.brk(ROM_d[7]));
  PullDown #(.Bits(16)) pulldown_1 (.out({pulldown_1_out, pulldown_1_out_2}));
  // Probe PC on CTRL_2_p3
  EEPROM #(.AddrBits(16), .Bits(16)) ROM (
    .A(CTRL_2_p3), .CS(1'b1), .WE(1'b0), .OE(nreset),
    .D({ROM_d[7], ROM_d_2, ROM_d[4:2], D_REGISTER_q[8], ROM_d[0], pulldown_1_out_2}));
  SixteenSeg sixteenseg_1 (
    .led({ROM_d[7], ROM_d_2, ROM_d[4:2], D_REGISTER_q[8], ROM_d[0], pulldown_1_out_2}), .dp(1'b0));
  SixteenSeg sixteenseg_2 (.led(in_8), .dp(1'b0));
  // Probe ROM on {pulldown_1_out, pulldown_1_out_2}
  // tom_1_ctrl CTRL_3: pin names not known; wires that end beside it: nclk, pulldown_1_out_2, pulldown_1_out
  // Probe CTRL on {ROM_d[7], ROM_d_2, ROM_d[4:2], D_REGISTER_q[8], ROM_d[0]}
  Decoder #(.Selector_Bits(2)) decoder_1 (
    .sel(ROM_d_2), .out_0(decoder_1_out_0), .out_1(decoder_1_out_1), .out_2(decoder_1_out_2),
    .out_3(decoder_1_out_3));
  assign {driver_2_out_2, driver_2_out} = decoder_1_out_0 ? {pulldown_1_out, pulldown_1_out_2} : 16'bz;  // Driver driver_2
  // Probe tos_bus on {driver_2_out_2, driver_2_out}
  and and_2 (and_2_out, ROM_d[4], clk);
  tom_1_273 TOS_LOW (.nCLR(nreset), .DATA(driver_2_out), .CLK(nclk), .OUT(TOS_LOW_out));
  tom_1_273 TOS_HIGH (.nCLR(nreset), .DATA(driver_2_out_2), .CLK(nclk), .OUT(TOS_HIGH_out));
  not not_2 (not_2_out, D_REGISTER_q[8]);
  and and_3 (and_3_out, ~D_REGISTER_q[8], and_2_out);  // And
  and and_4 (and_4_out, ~not_2_out, and_2_out);  // And
  tom_1_d_r D_REGISTER (
    .nENP(1'b0), .nCCLR(nreset), .RCK(clk), .R_nC(1'b0), .nG(D_REGISTER_q[8]), .nLOAD(1'b1), .nENT(1'b0),
    .U_nD(ROM_d[2]), .D(in_2), .CCK(and_3_out), .Q(D_REGISTER_q[7:0]));
  // Probe CCK on and_2_out
  tom_1_d_r R_REGISTER (
    .nENP(1'b0), .nCCLR(nreset), .RCK(clk), .R_nC(1'b0), .nG(not_2_out), .nLOAD(1'b1), .nENT(1'b0),
    .U_nD(ROM_d[2]), .D(in_3), .CCK(and_4_out), .Q(D_REGISTER_q[7:0]));
  assign {driverinvsel_1_out_2, driverinvsel_1_out} = ~ROM_d[0] ? {TOS_HIGH_out, TOS_LOW_out} : 16'bz;  // DriverInvSel driverinvsel_1
  // Probe TOS on {driverinvsel_1_out_2, driverinvsel_1_out}
  tom_1_is0 nTOS_eq__eq_0 (.\input ({driverinvsel_1_out_2, driverinvsel_1_out}), .nis0(nTOS_eq__eq_0_nis0));
  SixteenSeg sixteenseg_3 (.led({driverinvsel_1_out_2, driverinvsel_1_out}), .dp(1'b0));
  // Probe dr on D_REGISTER_q[7:0]
  LED led_1 (.in(nTOS_eq__eq_0_nis0));
  not not_3 (npulse, clk);
  not not_4 (not_4_out, decoder_1_out_1);
  and and_5 (and_5_out, not_4_out, ROM_d[3]);
  not not_5 (not_5_out, ROM_d[3]);
  LED led_2 (.in(npulse));
  // Probe on npulse
  LED led_3 (.in(clk));
  D_FF d_ff_1 (.D(clk_2), .C(npulse), .Q(nclk), .nQ(clk_2));
  not not_6 (not_6_out, and_5_out);
  // Probe ~d/r on D_REGISTER_q[8]
  not not_7 (not_7_out, decoder_1_out_1);
  // tom_1_io I_O_LOW: pin names not known; wires that end beside it: driverinvsel_1_out, not_6_out, I_O_LOW_p3
  // tom_1_io I_O_HIGH: pin names not known; wires that end beside it: driverinvsel_1_out_2, not_6_out, I_O_HIGH_p3
  and and_6 (and_6_out, decoder_1_out_1, not_5_out);
  and and_7 (and_7_out, decoder_1_out_1, ROM_d[3]);
  LED led_4 (.in(nclk));
  LED led_5 (.in(clk_2));
  // Probe stack addr on D_REGISTER_q
  RAMSinglePortSel #(.AddrBits(9), .Bits(16)) STACK (
    .A(D_REGISTER_q), .CS(1'b1), .WE(ROM_d[3]), .OE(not_7_out), .D({I_O_HIGH_p3, I_O_LOW_p3}));
  RAMSinglePortSel #(.AddrBits(16), .Bits(16)) ramsingleportsel_1 (
    .A({driverinvsel_1_out_2, driverinvsel_1_out}), .CS(1'b1), .WE(and_6_out), .OE(and_7_out),
    .D({I_O_HIGH_p3, I_O_LOW_p3}));
  // Probe stack_bus on {I_O_HIGH_p3, I_O_LOW_p3}
  tom_1_nand NAND (
    .A({driverinvsel_1_out_2, driverinvsel_1_out}), .B({I_O_HIGH_p3, I_O_LOW_p3}), .Vin(decoder_1_out_3),
    .out({driver_2_out_2, driver_2_out}));
  // tom_1_add tom_1_add_1: pin names not known; wires that end beside it: {driverinvsel_1_out_2, driverinvsel_1_out}, {I_O_HIGH_p3, I_O_LOW_p3}, decoder_1_out_2, {driver_2_out_2, driver_2_out}

  assign pulse = clk;

  // Other names for the same wires on the sheet: clk_t = clk_2

  // Notes on the sheet:
  //   clk: Hz: 10000
  //   CTRLs needed until PC latching works
  //   contents of ROM (hex, n*v repeats v):
  //   0,100,1c55,c66,1c11,c22,1cff,cff,1000,6000,1c00,c01,1000,4000,1000,4000,1000,4100,
  //   1c00,c00,1000,8000
  //   This is implicity two ICs
  //   TOS
  //   Clock
endmodule
